// Logisim project project3.circ as structural Verilog: 9 circuits, main circuit main
module main (
);

  regfile regfile_1 ();  // open: rs_data, rt_data, rd_data, rs_select, rd_select, rt_select, write_enable
endmodule

module regfile (
  input  [4:0] rs_select,
  input  [4:0] rt_select,
  input  [4:0] rd_select,
  input  write_enable,
  input  [31:0] rd_data,
  output [31:0] rs_data,
  output [31:0] rt_data
);

  wire clock_1_out, demultiplexer_1_out1, demultiplexer_1_out2, demultiplexer_1_out3, demultiplexer_1_out4,
       demultiplexer_1_out5, demultiplexer_1_out6, demultiplexer_1_out7, demultiplexer_1_out8,
       demultiplexer_1_out9, demultiplexer_1_out10, demultiplexer_1_out11, demultiplexer_1_out12,
       demultiplexer_1_out13, demultiplexer_1_out14, demultiplexer_1_out15, demultiplexer_1_out16,
       demultiplexer_1_out17, demultiplexer_1_out18, demultiplexer_1_out19, demultiplexer_1_out20,
       demultiplexer_1_out21, demultiplexer_1_out22, demultiplexer_1_out23, demultiplexer_1_out24,
       demultiplexer_1_out25, demultiplexer_1_out26, demultiplexer_1_out27, demultiplexer_1_out28,
       demultiplexer_1_out29, demultiplexer_1_out30, demultiplexer_1_out31;
  wire [31:0] demultiplexer_2_out1, demultiplexer_2_out2, demultiplexer_2_out3, demultiplexer_2_out4,
       demultiplexer_2_out5, demultiplexer_2_out6, demultiplexer_2_out7, demultiplexer_2_out8,
       demultiplexer_2_out9, demultiplexer_2_out10, demultiplexer_2_out11, demultiplexer_2_out12,
       demultiplexer_2_out13, demultiplexer_2_out14, demultiplexer_2_out15, demultiplexer_2_out16,
       demultiplexer_2_out17, demultiplexer_2_out18, demultiplexer_2_out19, demultiplexer_2_out20,
       demultiplexer_2_out21, demultiplexer_2_out22, demultiplexer_2_out23, demultiplexer_2_out24,
       demultiplexer_2_out25, demultiplexer_2_out26, demultiplexer_2_out27, demultiplexer_2_out28,
       demultiplexer_2_out29, demultiplexer_2_out30, demultiplexer_2_out31, r0_q, r2_q, r3_q, r4_q, r5_q,
       r6_q, r7_q, r8_q, r9_q, r10_q, r11_q, r12_q, r13_q, r14_q, r15_q, r16_q, r17_q, r18_q, r19_q, r20_q,
       r21_q, r22_q, r23_q, r24_q, r25_q, r26_q, r27_q, r28_q, r29_q, r30_q, r31_q;

  Clock clock_1 (.out(clock_1_out));
  Demultiplexer #(.enable("false"), .select(5)) demultiplexer_1 (
    .out1(demultiplexer_1_out1), .out2(demultiplexer_1_out2), .out3(demultiplexer_1_out3),
    .out4(demultiplexer_1_out4), .out5(demultiplexer_1_out5), .out6(demultiplexer_1_out6),
    .out7(demultiplexer_1_out7), .out8(demultiplexer_1_out8), .out9(demultiplexer_1_out9),
    .out10(demultiplexer_1_out10), .out11(demultiplexer_1_out11), .out12(demultiplexer_1_out12),
    .out13(demultiplexer_1_out13), .out14(demultiplexer_1_out14), .out15(demultiplexer_1_out15),
    .out16(demultiplexer_1_out16), .out17(demultiplexer_1_out17), .out18(demultiplexer_1_out18),
    .out19(demultiplexer_1_out19), .out20(demultiplexer_1_out20), .out21(demultiplexer_1_out21),
    .out22(demultiplexer_1_out22), .out23(demultiplexer_1_out23), .out24(demultiplexer_1_out24),
    .out25(demultiplexer_1_out25), .out26(demultiplexer_1_out26), .out27(demultiplexer_1_out27),
    .out28(demultiplexer_1_out28), .out29(demultiplexer_1_out29), .out30(demultiplexer_1_out30),
    .out31(demultiplexer_1_out31), .in(write_enable), .sel(rd_select));  // open: out0
  Demultiplexer #(.enable("false"), .select(5), .width(32)) demultiplexer_2 (
    .out1(demultiplexer_2_out1), .out2(demultiplexer_2_out2), .out3(demultiplexer_2_out3),
    .out4(demultiplexer_2_out4), .out5(demultiplexer_2_out5), .out6(demultiplexer_2_out6),
    .out7(demultiplexer_2_out7), .out8(demultiplexer_2_out8), .out9(demultiplexer_2_out9),
    .out10(demultiplexer_2_out10), .out11(demultiplexer_2_out11), .out12(demultiplexer_2_out12),
    .out13(demultiplexer_2_out13), .out14(demultiplexer_2_out14), .out15(demultiplexer_2_out15),
    .out16(demultiplexer_2_out16), .out17(demultiplexer_2_out17), .out18(demultiplexer_2_out18),
    .out19(demultiplexer_2_out19), .out20(demultiplexer_2_out20), .out21(demultiplexer_2_out21),
    .out22(demultiplexer_2_out22), .out23(demultiplexer_2_out23), .out24(demultiplexer_2_out24),
    .out25(demultiplexer_2_out25), .out26(demultiplexer_2_out26), .out27(demultiplexer_2_out27),
    .out28(demultiplexer_2_out28), .out29(demultiplexer_2_out29), .out30(demultiplexer_2_out30),
    .out31(demultiplexer_2_out31), .in(rd_data), .sel(rd_select));  // open: out0
  Register #(.width(32)) r0 (
    .D(demultiplexer_2_out1), .en(demultiplexer_1_out1), .clk(clock_1_out), .Q(r0_q));  // open: clr
  Register #(.width(32)) r2 (
    .D(demultiplexer_2_out2), .en(demultiplexer_1_out2), .clk(clock_1_out), .Q(r2_q));  // open: clr
  Register #(.width(32)) r3 (
    .D(demultiplexer_2_out3), .en(demultiplexer_1_out3), .clk(clock_1_out), .Q(r3_q));  // open: clr
  Register #(.width(32)) r4 (
    .D(demultiplexer_2_out4), .en(demultiplexer_1_out4), .clk(clock_1_out), .Q(r4_q));  // open: clr
  Register #(.width(32)) r5 (
    .D(demultiplexer_2_out5), .en(demultiplexer_1_out5), .clk(clock_1_out), .Q(r5_q));  // open: clr
  Register #(.width(32)) r6 (
    .D(demultiplexer_2_out6), .en(demultiplexer_1_out6), .clk(clock_1_out), .Q(r6_q));  // open: clr
  Register #(.width(32)) r7 (
    .D(demultiplexer_2_out7), .en(demultiplexer_1_out7), .clk(clock_1_out), .Q(r7_q));  // open: clr
  Register #(.width(32)) r8 (
    .D(demultiplexer_2_out8), .en(demultiplexer_1_out8), .clk(clock_1_out), .Q(r8_q));  // open: clr
  Multiplexer #(.enable("false"), .select(5), .width(32)) multiplexer_1 (
    .in0({32{1'b0}}), .in1(r0_q), .in2(r2_q), .in3(r3_q), .in4(r4_q), .in5(r5_q), .in6(r6_q), .in7(r7_q),
    .in8(r8_q), .in9(r9_q), .in10(r10_q), .in11(r11_q), .in12(r12_q), .in13(r13_q), .in14(r14_q),
    .in15(r15_q), .in16(r16_q), .in17(r17_q), .in18(r18_q), .in19(r19_q), .in20(r20_q), .in21(r21_q),
    .in22(r22_q), .in23(r23_q), .in24(r24_q), .in25(r25_q), .in26(r26_q), .in27(r27_q), .in28(r28_q),
    .in29(r29_q), .in30(r30_q), .in31(r31_q), .out(rs_data), .sel(rs_select));
  Register #(.width(32)) r9 (
    .D(demultiplexer_2_out9), .en(demultiplexer_1_out9), .clk(clock_1_out), .Q(r9_q));  // open: clr
  Register #(.width(32)) r10 (
    .D(demultiplexer_2_out10), .en(demultiplexer_1_out10), .clk(clock_1_out), .Q(r10_q));  // open: clr
  Register #(.width(32)) r11 (
    .D(demultiplexer_2_out11), .en(demultiplexer_1_out11), .clk(clock_1_out), .Q(r11_q));  // open: clr
  Register #(.width(32)) r12 (
    .D(demultiplexer_2_out12), .en(demultiplexer_1_out12), .clk(clock_1_out), .Q(r12_q));  // open: clr
  Register #(.width(32)) r13 (
    .D(demultiplexer_2_out13), .en(demultiplexer_1_out13), .clk(clock_1_out), .Q(r13_q));  // open: clr
  Register #(.width(32)) r14 (
    .D(demultiplexer_2_out14), .en(demultiplexer_1_out14), .clk(clock_1_out), .Q(r14_q));  // open: clr
  Register #(.width(32)) r15 (
    .D(demultiplexer_2_out15), .en(demultiplexer_1_out15), .clk(clock_1_out), .Q(r15_q));  // open: clr
  Register #(.width(32)) r16 (
    .D(demultiplexer_2_out16), .en(demultiplexer_1_out16), .clk(clock_1_out), .Q(r16_q));  // open: clr
  Multiplexer #(.enable("false"), .select(5), .width(32)) multiplexer_2 (
    .in0({32{1'b0}}), .in1(r0_q), .in2(r2_q), .in3(r3_q), .in4(r4_q), .in5(r5_q), .in6(r6_q), .in7(r7_q),
    .in8(r8_q), .in9(r9_q), .in10(r10_q), .in11(r11_q), .in12(r12_q), .in13(r13_q), .in14(r14_q),
    .in15(r15_q), .in16(r16_q), .in17(r17_q), .in18(r18_q), .in19(r19_q), .in20(r20_q), .in21(r21_q),
    .in22(r22_q), .in23(r23_q), .in24(r24_q), .in25(r25_q), .in26(r26_q), .in27(r27_q), .in28(r28_q),
    .in29(r29_q), .in30(r30_q), .in31(r31_q), .out(rt_data), .sel(rt_select));
  Register #(.width(32)) r17 (
    .D(demultiplexer_2_out17), .en(demultiplexer_1_out17), .clk(clock_1_out), .Q(r17_q));  // open: clr
  Register #(.width(32)) r18 (
    .D(demultiplexer_2_out18), .en(demultiplexer_1_out18), .clk(clock_1_out), .Q(r18_q));  // open: clr
  Register #(.width(32)) r19 (
    .D(demultiplexer_2_out19), .en(demultiplexer_1_out19), .clk(clock_1_out), .Q(r19_q));  // open: clr
  Register #(.width(32)) r20 (
    .D(demultiplexer_2_out20), .en(demultiplexer_1_out20), .clk(clock_1_out), .Q(r20_q));  // open: clr
  Register #(.width(32)) r21 (
    .D(demultiplexer_2_out21), .en(demultiplexer_1_out21), .clk(clock_1_out), .Q(r21_q));  // open: clr
  Register #(.width(32)) r22 (
    .D(demultiplexer_2_out22), .en(demultiplexer_1_out22), .clk(clock_1_out), .Q(r22_q));  // open: clr
  Register #(.width(32)) r23 (
    .D(demultiplexer_2_out23), .en(demultiplexer_1_out23), .clk(clock_1_out), .Q(r23_q));  // open: clr
  Register #(.width(32)) r24 (
    .D(demultiplexer_2_out24), .en(demultiplexer_1_out24), .clk(clock_1_out), .Q(r24_q));  // open: clr
  Register #(.width(32)) r25 (
    .D(demultiplexer_2_out25), .en(demultiplexer_1_out25), .clk(clock_1_out), .Q(r25_q));  // open: clr
  Register #(.width(32)) r26 (
    .D(demultiplexer_2_out26), .en(demultiplexer_1_out26), .clk(clock_1_out), .Q(r26_q));  // open: clr
  Register #(.width(32)) r27 (
    .D(demultiplexer_2_out27), .en(demultiplexer_1_out27), .clk(clock_1_out), .Q(r27_q));  // open: clr
  Register #(.width(32)) r28 (
    .D(demultiplexer_2_out28), .en(demultiplexer_1_out28), .clk(clock_1_out), .Q(r28_q));  // open: clr
  Register #(.width(32)) r29 (
    .D(demultiplexer_2_out29), .en(demultiplexer_1_out29), .clk(clock_1_out), .Q(r29_q));  // open: clr
  Register #(.width(32)) r30 (
    .D(demultiplexer_2_out30), .en(demultiplexer_1_out30), .clk(clock_1_out), .Q(r30_q));  // open: clr
  Register #(.width(32)) r31 (
    .D(demultiplexer_2_out31), .en(demultiplexer_1_out31), .clk(clock_1_out), .Q(r31_q));  // open: clr
  // Probe on r31_q
endmodule

module ALU (
  input  [31:0] INN1,
  input  [31:0] IN2,
  input  [3:0] operation_select,
  input  Mult_write,
  input  Multdiv_select,
  output [31:0] Out1,
  output equals
);

  wire clock_1_out, comparator_1_lt;
  wire [4:0] bit_extender_1_out;
  wire [31:0] adder_1_out, bit_extender_2_out, divider_1_out, divider_1_rem, MFHI_q, MFLO_q,
       multiplexer_1_out, multiplexer_2_out, multiplier_1_cout, multiplier_1_out, shifter_1_out,
       shifter_2_out, subtractor_1_out;

  Bit_Extender #(.in_width(32), .out_width(5), .\type ("zero")) bit_extender_1 (.in(IN2), .out(bit_extender_1_out));
  assign bit_extender_2_out = {{31{1'b0}}, comparator_1_lt};  // Bit_Extender bit_extender_2
  Adder #(.width(32)) adder_1 (.a(INN1), .b(IN2), .out(adder_1_out));  // open: cin, cout
  Subtractor #(.width(32)) subtractor_1 (.a(INN1), .b(IN2), .out(subtractor_1_out));  // open: bin, bout
  Multiplier #(.width(32)) multiplier_1 (
    .a(INN1), .b(IN2), .out(multiplier_1_out), .cout(multiplier_1_cout));  // open: cin
  Divider #(.width(32)) divider_1 (.a(INN1), .b(IN2), .out(divider_1_out), .rem(divider_1_rem));  // open: upper
  Comparator #(.width(32)) comparator_1 (.a(INN1), .b(IN2), .eq(equals), .lt(comparator_1_lt));  // open: gt
  Shifter #(.width(32)) shifter_1 (.in(INN1), .\dist (bit_extender_1_out), .out(shifter_1_out));
  Shifter #(.shift("lr"), .width(32)) shifter_2 (.in(INN1), .\dist (bit_extender_1_out), .out(shifter_2_out));
  Multiplexer #(.enable("false"), .width(32)) multiplexer_1 (
    .in0(multiplier_1_cout), .in1(divider_1_rem), .out(multiplexer_1_out), .sel(Multdiv_select));
  Multiplexer #(.enable("false"), .width(32)) multiplexer_2 (
    .in0(multiplier_1_out), .in1(divider_1_out), .out(multiplexer_2_out), .sel(Multdiv_select));
  Clock clock_1 (.out(clock_1_out));
  Register #(.width(32)) MFHI (.D(multiplexer_1_out), .en(Mult_write), .clk(clock_1_out), .Q(MFHI_q));  // open: clr
  Register #(.width(32)) MFLO (.D(multiplexer_2_out), .en(Mult_write), .clk(clock_1_out), .Q(MFLO_q));  // open: clr
  Multiplexer #(.enable("false"), .select(4), .width(32)) multiplexer_3 (
    .in0(adder_1_out), .in1(subtractor_1_out), .in2(bit_extender_2_out), .in3(shifter_1_out),
    .in4(shifter_2_out), .in5(MFHI_q), .in6(MFLO_q), .out(Out1), .sel(operation_select));  // open: in7, in8, in9, in10, in11, in12, in13, in14, in15

  // Notes on the sheet:
  //   checked: add,Sub, slt,mult, div, mflo,mfhi,sll,srl
  //   0- mult/ sll, 1- div/srl
  //   0 - add, 1- sub, 2-  compare, 3- sll, 4- srl, 5- get from hi, 6- get from lo
endmodule

module CPU (
  input  [31:0] DataBusIn,
  input  in_2,
  output [31:0] Data_Bus,
  output Data_Write_E,
  output [15:0] Address,
  output Mem_Write_e
);

  wire alu_1_equals, beq_out, bne_out, clock_1_out, control_1_all_jump, control_1_beq_switch,
       control_1_bne_switch, control_1_immi_select, control_1_jal_jalr, control_1_jr_jalr,
       control_1_mult_write, control_1_multdiv_select, control_1_we_out, not_1_out, or_1_out;
  wire [3:0] control_1_operation_select;
  wire [4:0] control_1_rd_select, control_1_rs_select, control_1_rt_selectt;
  wire [15:0] bit_extender_1_out, bit_extender_2_out, shifter_3_out;
  wire [31:0] adder_1_out, adder_2_out, alu_1_out1, control_1_immediate, multiplexer_1_out,
       multiplexer_2_out, multiplexer_3_out, multiplexer_4_out, multiplexer_5_out, multiplexer_6_out, pc_q,
       regfile_1_rs_data, rom_1_data, shifter_1_out, shifter_2_out;

  Adder #(.width(32)) adder_1 (.a(pc_q), .b(32'h4), .out(adder_1_out));  // open: cin, cout
  Shifter #(.width(32)) shifter_1 (.in(control_1_immediate), .\dist (5'b00010), .out(shifter_1_out));
  and beq (beq_out, control_1_beq_switch, alu_1_equals);
  Adder #(.width(32)) adder_2 (.a(adder_1_out), .b(shifter_1_out), .out(adder_2_out));  // open: cin, cout
  Shifter #(.width(32)) shifter_2 (.in(control_1_immediate), .\dist (5'b00010), .out(shifter_2_out));
  or or_1 (or_1_out, beq_out, bne_out);
  Multiplexer #(.enable("false"), .width(32)) multiplexer_1 (
    .in0(adder_1_out), .in1(adder_2_out), .out(multiplexer_1_out), .sel(or_1_out));
  Multiplexer #(.enable("false"), .width(32)) multiplexer_2 (
    .in0(shifter_2_out), .in1(regfile_1_rs_data), .out(multiplexer_2_out), .sel(control_1_jr_jalr));
  Multiplexer #(.enable("false"), .width(32)) multiplexer_3 (
    .in0(multiplexer_1_out), .in1(multiplexer_2_out), .out(multiplexer_3_out), .sel(control_1_all_jump));
  Register #(.width(32)) pc (.D(multiplexer_3_out), .en(1'b1), .clk(clock_1_out), .Q(pc_q), .clr(in_2));
  Clock clock_1 (.out(clock_1_out));
  and bne (bne_out, control_1_bne_switch, not_1_out);
  Bit_Extender #(.in_width(32)) bit_extender_1 (.in(pc_q), .out(bit_extender_1_out));
  ROM #(.addrWidth(16), .dataWidth(32)) rom_1 (.addr(shifter_3_out), .data(rom_1_data));
  Shifter #(.shift("lr"), .width(16)) shifter_3 (.in(bit_extender_1_out), .\dist (4'b0010), .out(shifter_3_out));
  Control control_1 (
    .instruction(rom_1_data), .rd_select(control_1_rd_select), .immediate(control_1_immediate),
    .rs_select(control_1_rs_select), .rt_selectt(control_1_rt_selectt),
    .Operation_select(control_1_operation_select), .Write_enable(Data_Write_E),
    .Multdiv_select(control_1_multdiv_select), .Mult_write(control_1_mult_write),
    .Immi_select(control_1_immi_select), .we_out(control_1_we_out), .write_enable_write(Mem_Write_e),
    .jal_jalr(control_1_jal_jalr), .jr_jalr(control_1_jr_jalr), .all_jump(control_1_all_jump),
    .beq_switch(control_1_beq_switch), .bne_switch(control_1_bne_switch));  // open: sa
  Multiplexer #(.enable("false"), .width(32)) multiplexer_4 (
    .in0(multiplexer_6_out), .in1(adder_1_out), .out(multiplexer_4_out), .sel(control_1_jal_jalr));
  regfile regfile_1 (
    .rs_data(regfile_1_rs_data), .rt_data(Data_Bus), .rd_data(multiplexer_4_out),
    .rs_select(control_1_rs_select), .rd_select(control_1_rd_select), .rt_select(control_1_rt_selectt),
    .write_enable(Data_Write_E));
  not not_1 (not_1_out, alu_1_equals);
  Multiplexer #(.enable("false"), .width(32)) multiplexer_5 (
    .in0(Data_Bus), .in1(control_1_immediate), .out(multiplexer_5_out), .sel(control_1_immi_select));
  ALU alu_1 (
    .Out1(alu_1_out1), .equals(alu_1_equals), .operation_select(control_1_operation_select),
    .Multdiv_select(control_1_multdiv_select), .INN1(regfile_1_rs_data), .IN2(multiplexer_5_out),
    .Mult_write(control_1_mult_write));
  Multiplexer #(.enable("false"), .width(32)) multiplexer_6 (
    .in0(alu_1_out1), .in1(DataBusIn), .out(multiplexer_6_out), .sel(control_1_we_out));
  Bit_Extender #(.in_width(32), .\type ("zero")) bit_extender_2 (.in(alu_1_out1), .out(bit_extender_2_out));
  Shifter #(.shift("lr"), .width(16)) shifter_4 (.in(bit_extender_2_out), .\dist (4'b0010), .out(Address));

  // Notes on the sheet:
  //   branch offset
  //   contents of rom_1 (hex, n*v repeats v):
  //   20840004 20080001 ac890000 8d440000 3e00008
endmodule

// sw
module Control (
  input  [31:0] instruction,
  output [4:0] rd_select,
  output [31:0] immediate,
  output [4:0] rs_select,
  output [4:0] rt_selectt,
  output [4:0] sa,
  output [3:0] Operation_select,
  output Write_enable,
  output Multdiv_select,
  output Mult_write,
  output Immi_select,
  output we_out,
  output write_enable_write,
  output jal_jalr,
  output jr_jalr,
  output all_jump,
  output beq_switch,
  output bne_switch
);

  wire ADD_out, ADDI_out, and_29_out, and_30_out, and_31_out, and_32_out, and_33_out, and_34_out, and_39_out,
       and_41_out, and_42_out, and_43_out, and_45_out, and_46_out, and_49_out, DIV_out, Jal_out, JALR_out,
       jr_out, Jump_out, MFHI_out, MFLO_out, MULT_out, not_1_out, not_2_out, not_3_out, not_4_out, not_5_out,
       not_6_out, not_7_out, not_8_out, not_9_out, not_10_out, not_11_out, not_12_out, not_13_out,
       not_14_out, not_15_out, not_16_out, not_17_out, not_18_out, not_19_out, not_20_out, not_21_out,
       not_22_out, not_23_out, not_24_out, not_25_out, not_26_out, not_27_out, not_28_out, not_29_out,
       not_30_out, not_31_out, not_32_out, not_33_out, not_34_out, not_35_out, not_36_out, not_37_out,
       not_38_out, not_39_out, not_40_out, not_41_out, not_42_out, not_43_out, not_44_out, not_45_out,
       not_46_out, not_47_out, not_48_out, not_49_out, not_50_out, not_51_out, not_52_out, not_53_out,
       not_54_out, not_55_out, not_56_out, not_57_out, not_58_out, not_59_out, not_60_out, not_61_out,
       not_62_out, not_63_out, not_64_out, not_65_out, not_66_out, not_67_out, not_68_out, not_69_out,
       not_70_out, not_71_out, not_72_out, not_73_out, not_74_out, not_75_out, not_76_out, not_77_out,
       not_78_out, not_79_out, not_80_out, not_81_out, not_82_out, Op0_out, or_2_out, or_3_out, or_4_out,
       or_9_out, shiftLL_out, ShiftRL_out, SLT_out, SUB_out;
  wire [3:0] and_35_out, and_36_out, and_37_out, and_38_out, and_44_out, and_47_out, and_48_out,
       bit_extender_19_out, bit_extender_20_out, bit_extender_21_out, bit_extender_22_out,
       bit_extender_24_out, bit_extender_25_out, bit_extender_28_out;
  wire [4:0] and_2_out, and_3_out, and_4_out, and_5_out, and_6_out, and_8_out, and_9_out, and_10_out,
       and_12_out, and_13_out, and_14_out, and_16_out, and_17_out, and_19_out, and_20_out, and_22_out,
       and_23_out, and_24_out, and_25_out, and_26_out, and_28_out, and_40_out, and_50_out, and_51_out,
       bit_extender_1_out, bit_extender_4_out, bit_extender_5_out, bit_extender_8_out, bit_extender_9_out,
       bit_extender_10_out, bit_extender_13_out, bit_extender_14_out, bit_extender_17_out,
       bit_extender_18_out, bit_extender_23_out, bit_extender_33_out, bit_extender_34_out;
  wire [15:0] and_1_out, and_11_out, and_15_out, and_18_out, and_27_out, bit_extender_2_out,
       bit_extender_3_out, bit_extender_7_out, bit_extender_11_out, bit_extender_16_out;
  wire [25:0] and_7_out, and_21_out, bit_extender_6_out, bit_extender_12_out;
  wire [31:0] bit_extender_15_out, bit_extender_26_out, bit_extender_27_out, bit_extender_29_out,
       bit_extender_30_out, bit_extender_31_out, bit_extender_32_out, bit_extender_35_out;

  assign and_1_out = instruction[15:0] & bit_extender_2_out;  // AND_Gate and_1, 16 bits wide
  assign bit_extender_1_out = {{4{or_3_out}}, or_3_out};  // Bit_Extender bit_extender_1
  assign bit_extender_2_out = {{11{bit_extender_4_out[4]}}, bit_extender_4_out};  // Bit_Extender bit_extender_2
  not not_1 (not_1_out, instruction[28]);
  not not_2 (not_2_out, instruction[29]);
  not not_3 (not_3_out, instruction[30]);
  and lw (we_out, instruction[26], instruction[27], not_1_out, not_2_out, not_3_out, instruction[31]);
  not not_4 (not_4_out, instruction[28]);
  not not_5 (not_5_out, instruction[30]);
  not not_6 (not_6_out, instruction[26]);
  not not_7 (not_7_out, instruction[28]);
  not not_8 (not_8_out, instruction[29]);
  not not_9 (not_9_out, instruction[30]);
  not not_10 (not_10_out, instruction[31]);
  not not_11 (not_11_out, instruction[28]);
  not not_12 (not_12_out, instruction[29]);
  not not_13 (not_13_out, instruction[30]);
  not not_14 (not_14_out, instruction[31]);
  not not_15 (not_15_out, instruction[26]);
  not not_16 (not_16_out, instruction[27]);
  not not_17 (not_17_out, instruction[29]);
  not not_18 (not_18_out, instruction[30]);
  not not_19 (not_19_out, instruction[31]);
  not not_20 (not_20_out, instruction[27]);
  not not_21 (not_21_out, instruction[29]);
  not not_22 (not_22_out, instruction[30]);
  not not_23 (not_23_out, instruction[31]);
  and sw (write_enable_write, instruction[26], instruction[27], not_4_out, instruction[29], not_5_out, instruction[31]);
  and Jump (Jump_out, not_6_out, instruction[27], not_7_out, not_8_out, not_9_out, not_10_out);
  and Jal (Jal_out, instruction[26], instruction[27], not_11_out, not_12_out, not_13_out, not_14_out);
  and Beq (beq_switch, not_15_out, not_16_out, instruction[28], not_17_out, not_18_out, not_19_out);
  and bne (bne_switch, instruction[26], not_20_out, instruction[28], not_21_out, not_22_out, not_23_out);
  assign and_2_out = bit_extender_1_out & instruction[25:21];  // AND_Gate and_2, 5 bits wide
  assign and_3_out = bit_extender_1_out & instruction[20:16];  // AND_Gate and_3, 5 bits wide
  assign and_4_out = bit_extender_1_out & instruction[15:11];  // AND_Gate and_4, 5 bits wide
  assign and_5_out = bit_extender_1_out & instruction[10:6];  // AND_Gate and_5, 5 bits wide
  assign and_6_out = instruction[25:21] & bit_extender_4_out;  // AND_Gate and_6, 5 bits wide
  assign bit_extender_3_out = {{11{bit_extender_5_out[4]}}, bit_extender_5_out};  // Bit_Extender bit_extender_3
  assign bit_extender_4_out = {{4{we_out}}, we_out};  // Bit_Extender bit_extender_4
  assign bit_extender_5_out = {{4{write_enable_write}}, write_enable_write};  // Bit_Extender bit_extender_5
  assign and_7_out = {instruction[25:21], instruction[16], instruction[17], instruction[18], instruction[19], instruction[20], instruction[15:0]} & bit_extender_6_out;  // AND_Gate and_7, 26 bits wide
  assign bit_extender_6_out = {{25{Jump_out}}, Jump_out};  // Bit_Extender bit_extender_6
  assign and_8_out = instruction[20:16] & bit_extender_9_out;  // AND_Gate and_8, 5 bits wide
  assign and_9_out = instruction[25:21] & bit_extender_9_out;  // AND_Gate and_9, 5 bits wide
  assign and_10_out = instruction[20:16] & bit_extender_4_out;  // AND_Gate and_10, 5 bits wide
  not not_24 (not_24_out, instruction[0]);
  not not_25 (not_25_out, instruction[1]);
  not not_26 (not_26_out, instruction[2]);
  not not_27 (not_27_out, instruction[4]);
  assign bit_extender_7_out = {{15{bne_switch}}, bne_switch};  // Bit_Extender bit_extender_7
  not not_28 (not_28_out, instruction[3]);
  not not_29 (not_29_out, instruction[5]);
  assign and_11_out = instruction[15:0] & bit_extender_3_out;  // AND_Gate and_11, 16 bits wide
  assign and_12_out = instruction[20:16] & bit_extender_5_out;  // AND_Gate and_12, 5 bits wide
  assign and_13_out = instruction[25:21] & bit_extender_5_out;  // AND_Gate and_13, 5 bits wide
  assign bit_extender_8_out = {{4{beq_switch}}, beq_switch};  // Bit_Extender bit_extender_8
  and shiftLL (shiftLL_out, not_24_out, not_25_out, not_26_out, not_28_out, not_27_out, not_29_out);
  assign bit_extender_9_out = {{4{ADDI_out}}, ADDI_out};  // Bit_Extender bit_extender_9
  assign bit_extender_10_out = {{4{bne_switch}}, bne_switch};  // Bit_Extender bit_extender_10
  assign and_14_out = instruction[25:21] & bit_extender_10_out;  // AND_Gate and_14, 5 bits wide
  assign bit_extender_11_out = {{11{1'b0}}, bit_extender_8_out};  // Bit_Extender bit_extender_11
  or or_1 (Immi_select, ShiftRL_out, we_out, ADDI_out, write_enable_write, and_29_out);
  assign and_15_out = instruction[15:0] & bit_extender_11_out;  // AND_Gate and_15, 16 bits wide
  assign and_16_out = instruction[20:16] & bit_extender_8_out;  // AND_Gate and_16, 5 bits wide
  assign and_17_out = instruction[25:21] & bit_extender_8_out;  // AND_Gate and_17, 5 bits wide
  not not_30 (not_30_out, instruction[0]);
  not not_31 (not_31_out, instruction[2]);
  not not_32 (not_32_out, instruction[3]);
  not not_33 (not_33_out, instruction[4]);
  not not_34 (not_34_out, instruction[27]);
  assign bit_extender_12_out = {{25{Jal_out}}, Jal_out};  // Bit_Extender bit_extender_12
  assign and_18_out = instruction[15:0] & bit_extender_7_out;  // AND_Gate and_18, 16 bits wide
  or or_2 (or_2_out, shiftLL_out, ShiftRL_out);
  not not_35 (not_35_out, instruction[5]);
  assign and_19_out = instruction[20:16] & bit_extender_10_out;  // AND_Gate and_19, 5 bits wide
  not not_36 (not_36_out, instruction[26]);
  not not_37 (not_37_out, instruction[28]);
  not not_38 (not_38_out, instruction[30]);
  not not_39 (not_39_out, instruction[31]);
  assign and_20_out = instruction[25:21] & bit_extender_17_out;  // AND_Gate and_20, 5 bits wide
  assign bit_extender_13_out = {{4{or_2_out}}, or_2_out};  // Bit_Extender bit_extender_13
  and ShiftRL (ShiftRL_out, not_30_out, instruction[1], not_31_out, not_32_out, not_33_out, not_35_out);
  not not_40 (not_40_out, instruction[0]);
  not not_41 (not_41_out, instruction[1]);
  not not_42 (not_42_out, instruction[2]);
  not not_43 (not_43_out, instruction[3]);
  not not_44 (not_44_out, instruction[4]);
  and ADDI (ADDI_out, not_36_out, not_34_out, not_37_out, instruction[29], not_38_out, not_39_out);
  assign and_21_out = {instruction[25:21], instruction[16], instruction[17], instruction[18], instruction[19], instruction[20], instruction[15:0]} & bit_extender_12_out;  // AND_Gate and_21, 26 bits wide
  assign bit_extender_14_out = {{4{Jal_out}}, Jal_out};  // Bit_Extender bit_extender_14
  not not_45 (not_45_out, instruction[0]);
  not not_46 (not_46_out, instruction[2]);
  not not_47 (not_47_out, instruction[3]);
  not not_48 (not_48_out, instruction[4]);
  // Probe on {5{1'b1}}
  assign and_22_out = bit_extender_13_out & instruction[20:16];  // AND_Gate and_22, 5 bits wide
  assign and_23_out = bit_extender_13_out & instruction[15:11];  // AND_Gate and_23, 5 bits wide
  assign bit_extender_15_out = {{16{and_18_out[15]}}, and_18_out};  // Bit_Extender bit_extender_15
  not not_49 (not_49_out, instruction[26]);
  not not_50 (not_50_out, instruction[27]);
  not not_51 (not_51_out, instruction[28]);
  not not_52 (not_52_out, instruction[29]);
  not not_53 (not_53_out, instruction[30]);
  not not_54 (not_54_out, instruction[31]);
  and ADD (ADD_out, not_40_out, not_41_out, not_42_out, not_43_out, not_44_out, instruction[5]);
  not not_55 (not_55_out, instruction[2]);
  or or_3 (or_3_out, ADD_out, SUB_out, SLT_out);
  and Op0 (Op0_out, not_49_out, not_50_out, not_51_out, not_52_out, not_53_out, not_54_out);
  and SUB (SUB_out, not_45_out, instruction[1], not_46_out, not_47_out, not_48_out, instruction[5]);
  not not_56 (not_56_out, instruction[0]);
  not not_57 (not_57_out, instruction[5]);
  assign bit_extender_16_out = {{15{ADDI_out}}, ADDI_out};  // Bit_Extender bit_extender_16
  assign and_24_out = {5{1'b1}} & bit_extender_14_out;  // AND_Gate and_24, 5 bits wide
  assign and_25_out = bit_extender_13_out & instruction[10:6];  // AND_Gate and_25, 5 bits wide
  assign and_26_out = instruction[25:21] & bit_extender_18_out;  // AND_Gate and_26, 5 bits wide
  and DIV (DIV_out, not_56_out, instruction[1], not_55_out, instruction[3], instruction[4], not_57_out);
  not not_58 (not_58_out, instruction[0]);
  not not_59 (not_59_out, instruction[1]);
  not not_60 (not_60_out, instruction[2]);
  not not_61 (not_61_out, instruction[5]);
  assign and_27_out = bit_extender_16_out & instruction[15:0];  // AND_Gate and_27, 16 bits wide
  assign and_28_out = instruction[20:16] & bit_extender_18_out;  // AND_Gate and_28, 5 bits wide
  not not_62 (not_62_out, instruction[0]);
  not not_63 (not_63_out, instruction[1]);
  not not_64 (not_64_out, instruction[2]);
  not not_65 (not_65_out, instruction[3]);
  assign bit_extender_17_out = {{4{and_46_out}}, and_46_out};  // Bit_Extender bit_extender_17
  or or_4 (or_4_out, DIV_out, MULT_out);
  assign bit_extender_18_out = {{4{or_4_out}}, or_4_out};  // Bit_Extender bit_extender_18
  and and_29 (and_29_out, shiftLL_out, Op0_out);
  and and_30 (and_30_out, ShiftRL_out, Op0_out);
  and and_31 (and_31_out, ADD_out, Op0_out);
  and and_32 (and_32_out, SUB_out, Op0_out);
  and and_33 (and_33_out, DIV_out, Op0_out);
  and MULT (MULT_out, not_58_out, not_59_out, not_60_out, instruction[3], instruction[4], not_61_out);
  not not_66 (not_66_out, instruction[5]);
  not not_67 (not_67_out, instruction[0]);
  not not_68 (not_68_out, instruction[2]);
  not not_69 (not_69_out, instruction[3]);
  assign bit_extender_19_out = {{3{and_29_out}}, and_29_out};  // Bit_Extender bit_extender_19
  assign bit_extender_20_out = {{3{and_30_out}}, and_30_out};  // Bit_Extender bit_extender_20
  assign bit_extender_21_out = {{3{and_31_out}}, and_31_out};  // Bit_Extender bit_extender_21
  assign bit_extender_22_out = {{3{and_32_out}}, and_32_out};  // Bit_Extender bit_extender_22
  and and_34 (and_34_out, MULT_out, Op0_out);
  and MFHI (MFHI_out, not_62_out, not_63_out, not_64_out, not_65_out, instruction[4], not_66_out);
  not not_70 (not_70_out, instruction[5]);
  not not_71 (not_71_out, instruction[0]);
  not not_72 (not_72_out, instruction[2]);
  not not_73 (not_73_out, instruction[4]);
  assign and_35_out = bit_extender_19_out & 4'b0011;  // AND_Gate and_35, 4 bits wide
  assign and_36_out = bit_extender_20_out & 4'b0100;  // AND_Gate and_36, 4 bits wide
  assign and_37_out = bit_extender_21_out & 4'b0000;  // AND_Gate and_37, 4 bits wide
  assign and_38_out = bit_extender_22_out & 4'b0001;  // AND_Gate and_38, 4 bits wide
  and MFLO (MFLO_out, not_67_out, instruction[1], not_68_out, not_69_out, instruction[4], not_70_out);
  not not_74 (not_74_out, instruction[0]);
  not not_75 (not_75_out, instruction[1]);
  not not_76 (not_76_out, instruction[2]);
  not not_77 (not_77_out, instruction[4]);
  not not_78 (not_78_out, instruction[5]);
  assign rd_select = and_51_out | and_12_out | and_4_out | and_23_out | and_24_out | and_40_out | and_8_out | and_10_out | and_20_out;  // OR_Gate or_5, 5 bits wide
  assign rs_select = and_14_out | and_6_out | and_20_out | and_2_out | and_26_out | and_9_out | and_13_out | and_50_out | and_17_out | and_22_out;  // OR_Gate or_6, 5 bits wide
  assign rt_selectt = and_10_out | and_16_out | and_3_out | and_28_out | and_8_out | and_12_out | and_19_out;  // OR_Gate or_7, 5 bits wide
  assign sa = and_5_out;  // OR_Gate or_8, 5 bits wide OR_Gate
  or or_9 (or_9_out, MFHI_out, MFLO_out);
  and and_39 (and_39_out, MFHI_out, Op0_out);
  and SLT (SLT_out, not_71_out, instruction[1], not_72_out, instruction[3], not_73_out, instruction[5]);
  assign bit_extender_23_out = {{4{or_9_out}}, or_9_out};  // Bit_Extender bit_extender_23
  and jr (jr_out, not_74_out, not_75_out, not_76_out, instruction[3], not_77_out, not_78_out);
  assign and_40_out = instruction[15:11] & bit_extender_23_out;  // AND_Gate and_40, 5 bits wide
  assign bit_extender_24_out = {{3{and_39_out}}, and_39_out};  // Bit_Extender bit_extender_24
  and and_41 (and_41_out, MFLO_out, Op0_out);
  not not_79 (not_79_out, instruction[1]);
  not not_80 (not_80_out, instruction[2]);
  not not_81 (not_81_out, instruction[4]);
  not not_82 (not_82_out, instruction[5]);
  and and_42 (and_42_out, and_33_out, 1'b1);
  and and_43 (and_43_out, and_34_out, 1'b0);
  assign and_44_out = bit_extender_24_out & 4'b0101;  // AND_Gate and_44, 4 bits wide
  assign bit_extender_25_out = {{3{and_41_out}}, and_41_out};  // Bit_Extender bit_extender_25
  and and_45 (and_45_out, SLT_out, Op0_out);
  and and_46 (and_46_out, Op0_out, jr_out);
  assign bit_extender_26_out = {{16{and_1_out[15]}}, and_1_out};  // Bit_Extender bit_extender_26
  assign bit_extender_27_out = {{16{and_11_out[15]}}, and_11_out};  // Bit_Extender bit_extender_27
  or or_10 (Multdiv_select, and_42_out, and_43_out);
  assign and_47_out = bit_extender_25_out & 4'b0110;  // AND_Gate and_47, 4 bits wide
  assign bit_extender_28_out = {{3{and_45_out}}, and_45_out};  // Bit_Extender bit_extender_28
  and JALR (JALR_out, instruction[0], not_79_out, not_80_out, instruction[3], not_81_out, not_82_out);
  assign bit_extender_29_out = {{27{and_25_out[4]}}, and_25_out};  // Bit_Extender bit_extender_29
  assign bit_extender_30_out = {{16{and_27_out[15]}}, and_27_out};  // Bit_Extender bit_extender_30
  assign Operation_select = and_35_out | and_36_out | and_37_out | and_38_out | and_44_out | and_47_out | and_48_out;  // OR_Gate or_11, 4 bits wide
  or or_12 (Write_enable, we_out, write_enable_write, and_33_out, ShiftRL_out, and_29_out, SLT_out, ADD_out, ADDI_out, jal_jalr, and_34_out, and_33_out, and_34_out, SUB_out);
  assign and_48_out = bit_extender_28_out & 4'b0010;  // AND_Gate and_48, 4 bits wide
  and and_49 (and_49_out, Op0_out, JALR_out);
  assign bit_extender_31_out = {{16{and_15_out[15]}}, and_15_out};  // Bit_Extender bit_extender_31
  assign bit_extender_32_out = {{6{and_21_out[25]}}, and_21_out};  // Bit_Extender bit_extender_32
  assign bit_extender_33_out = {{4{and_49_out}}, and_49_out};  // Bit_Extender bit_extender_33
  assign bit_extender_34_out = {{4{and_49_out}}, and_49_out};  // Bit_Extender bit_extender_34
  or or_13 (Mult_write, DIV_out, MULT_out);
  assign and_50_out = bit_extender_33_out & instruction[25:21];  // AND_Gate and_50, 5 bits wide
  assign bit_extender_35_out = {{6{and_7_out[25]}}, and_7_out};  // Bit_Extender bit_extender_35
  assign and_51_out = bit_extender_34_out & instruction[15:11];  // AND_Gate and_51, 5 bits wide
  assign immediate = bit_extender_29_out | bit_extender_26_out | bit_extender_27_out | bit_extender_30_out | bit_extender_32_out | bit_extender_31_out | bit_extender_35_out | bit_extender_15_out;  // OR_Gate or_14, 32 bits wide
  or or_15 (jal_jalr, Jal_out, and_49_out);
  or or_16 (jr_jalr, jr_out, JALR_out);
  or or_17 (all_jump, jal_jalr, jr_jalr, Jump_out);

  // Notes on the sheet:
  //   FUNCTION CODE
  //   OPCODE
  //   How many bits 
endmodule

module Main_Bus (
);

  wire clock_1_out, clock_2_out, cpu_1_data_write_e, cpu_1_mem_write_e, datamemoryblock_1_writetobus,
       keyboard_1_avail, keyboardcontroller_1_databuswrite, keyboardcontroller_1_keyboardread,
       terminalcontroller_1_termwriteenable;
  wire [6:0] keyboard_1_data, terminalcontroller_1_termbyteout;
  wire [15:0] cpu_1_address;
  wire [31:0] controlled_buffer_1_out, cpu_1_data_bus, datamemoryblock_1_datatobus,
       keyboardcontroller_1_databusout;

  Clock clock_1 (.out(clock_1_out));
  TTY tty_1 (
    .data(terminalcontroller_1_termbyteout), .clk(clock_1_out), .we(terminalcontroller_1_termwriteenable));  // open: clr
  Clock clock_2 (.out(clock_2_out));
  Keyboard keyboard_1 (
    .clk(clock_2_out), .re(keyboardcontroller_1_keyboardread), .avail(keyboard_1_avail),
    .data(keyboard_1_data));  // open: clr
  assign controlled_buffer_1_out = datamemoryblock_1_writetobus ? datamemoryblock_1_datatobus : 32'bz;  // Controlled_Buffer controlled_buffer_1
  DataMemoryBlock datamemoryblock_1 (
    .MemWriteEnable(cpu_1_mem_write_e), .AddressFromBus(cpu_1_address),
    .DataFromBus(controlled_buffer_1_out), .DataToBus(datamemoryblock_1_datatobus),
    .WriteToBus(datamemoryblock_1_writetobus));
  assign controlled_buffer_1_out = cpu_1_data_write_e ? cpu_1_data_bus : 32'bz;  // Controlled_Buffer controlled_buffer_2
  CPU cpu_1 (
    .DataBusIn(controlled_buffer_1_out), .Data_Bus(cpu_1_data_bus), .Data_Write_E(cpu_1_data_write_e),
    .Address(cpu_1_address), .Mem_Write_e(cpu_1_mem_write_e));  // open: in_2
  assign controlled_buffer_1_out = keyboardcontroller_1_databuswrite ? keyboardcontroller_1_databusout : 32'bz;  // Controlled_Buffer controlled_buffer_3
  KeyboardController keyboardcontroller_1 (
    .WriteEnable(cpu_1_mem_write_e), .DataBusIn(controlled_buffer_1_out), .AddressIn(cpu_1_address),
    .KeyboardKeyPresAvailable(keyboard_1_avail), .KeyboardIn(keyboard_1_data),
    .DataBusOut(keyboardcontroller_1_databusout), .DataBusWrite(keyboardcontroller_1_databuswrite),
    .KeyBoardRead(keyboardcontroller_1_keyboardread));
  TerminalController terminalcontroller_1 (
    .AddressIn(cpu_1_address), .DataBusIn(controlled_buffer_1_out), .WriteEnable(cpu_1_mem_write_e),
    .TermWriteEnable(terminalcontroller_1_termwriteenable), .TermByteOut(terminalcontroller_1_termbyteout));

  // Notes on the sheet:
  //   Address
  //   Data
  //   Read/Write
endmodule

module DataMemoryBlock (
  input  MemWriteEnable,
  input  [15:0] AddressFromBus,
  input  [31:0] DataFromBus,
  output [31:0] DataToBus,
  output WriteToBus
);

  wire clock_1_out, not_1_out, or_1_out;

  Comparator comparator_1 ();  // open: a, b, gt, eq, lt
  RAM #(.addrWidth(16), .dataWidth(32), .enables("line")) ram_1 (
    .addr(AddressFromBus), .we(MemWriteEnable), .clk(clock_1_out), .din(DataFromBus), .dout(DataToBus));
  Clock clock_1 (.out(clock_1_out));
  not not_1 (not_1_out, MemWriteEnable);
  and and_1 (WriteToBus, or_1_out, not_1_out);
  or or_1 (or_1_out, AddressFromBus[15], AddressFromBus[14], AddressFromBus[13], AddressFromBus[12], AddressFromBus[11], AddressFromBus[10], AddressFromBus[9], AddressFromBus[8]);
endmodule

module KeyboardController (
  input  WriteEnable,
  input  [31:0] DataBusIn,
  input  [15:0] AddressIn,
  input  KeyboardKeyPresAvailable,
  input  [6:0] KeyboardIn,
  output [31:0] DataBusOut,
  output DataBusWrite,
  output KeyBoardRead
);

  wire and_1_out, and_2_out, and_3_out, clock_1_out, not_1_out, not_2_out, not_3_out, not_4_out, not_5_out,
       not_6_out, not_7_out, not_8_out, not_9_out, not_10_out, not_11_out, not_12_out, not_13_out,
       not_14_out, not_15_out, not_16_out, not_17_out, not_18_out, or_1_out;
  wire [7:0] bit_extender_1_out;
  wire [31:0] bit_extender_2_out, multiplexer_1_out;

  not not_1 (not_1_out, AddressIn[0]);
  not not_2 (not_2_out, AddressIn[1]);
  not not_3 (not_3_out, AddressIn[2]);
  not not_4 (not_4_out, AddressIn[3]);
  not not_5 (not_5_out, AddressIn[5]);
  not not_6 (not_6_out, AddressIn[6]);
  not not_7 (not_7_out, AddressIn[7]);
  not not_8 (not_8_out, AddressIn[8]);
  not not_9 (not_9_out, AddressIn[9]);
  not not_10 (not_10_out, AddressIn[10]);
  not not_11 (not_11_out, AddressIn[11]);
  not not_12 (not_12_out, AddressIn[12]);
  not not_13 (not_13_out, AddressIn[13]);
  not not_14 (not_14_out, AddressIn[14]);
  not not_15 (not_15_out, AddressIn[15]);
  and and_1 (and_1_out, KeyboardKeyPresAvailable, not_18_out);
  and and_2 (and_2_out, not_1_out, not_2_out, not_3_out, not_4_out, AddressIn[4], not_5_out, not_6_out, not_7_out, not_8_out, not_9_out, not_10_out, not_11_out, not_12_out, not_13_out, not_14_out, not_15_out);
  not not_16 (not_16_out, and_2_out);
  not not_17 (not_17_out, WriteEnable);
  and and_3 (and_3_out, WriteEnable, and_2_out);
  and and_4 (KeyBoardRead, not_16_out, and_1_out);
  and and_5 (DataBusWrite, and_2_out, not_17_out);
  or or_1 (or_1_out, and_3_out, KeyBoardRead);
  Multiplexer #(.enable("false"), .width(32)) multiplexer_1 (
    .in0(bit_extender_2_out), .in1(DataBusIn), .out(multiplexer_1_out), .sel(and_2_out));
  Register #(.width(32)) register_1 (
    .D(multiplexer_1_out), .en(or_1_out), .clk(clock_1_out), .Q(DataBusOut));  // open: clr
  Clock clock_1 (.out(clock_1_out));
  not not_18 (not_18_out, DataBusOut[7]);
  assign bit_extender_1_out = {{1{1'b1}}, KeyboardIn};  // Bit_Extender bit_extender_1
  assign bit_extender_2_out = {{24{1'b0}}, bit_extender_1_out};  // Bit_Extender bit_extender_2
endmodule

module TerminalController (
  input  [15:0] AddressIn,
  input  [31:0] DataBusIn,
  input  WriteEnable,
  output TermWriteEnable,
  output [6:0] TermByteOut
);
endmodule
